// Logisim project ALU.circ as structural Verilog: 1 circuit, main circuit main
module main (
  input  [15:0] DR,
  input  CLK,
  input  [7:0] INPR,
  input  [6:0] INP_7,
  input  CLEAN,
  output LOAD,
  output [15:0] AC
);

  wire main_1_cout, main_2_cout, main_3_cout, main_4_cout, main_5_cout, main_6_cout, main_7_cout,
       main_8_cout, main_9_cout, main_10_cout, main_11_cout, main_12_cout, main_13_cout, main_14_cout,
       main_15_cout;

  or or_1 (LOAD, 1'b0, INP_7[6], INP_7[5], INP_7[4], INP_7[2], INP_7[1], INP_7[0], INP_7[3]);
  Alublock_main main_1 (
    .AND(INP_7[0]), .ADD(INP_7[1]), .DR(INP_7[2]), .INPR(INP_7[3]), .COM(INP_7[4]), .SHR(INP_7[5]),
    .SHL(INP_7[6]), .DR_i(DR[0]), .AC_i(AC[0]), .Cin(1'b0), .INPR_I(INPR[0]), .LD(LOAD), .CLK(CLK),
    .Cout(main_1_cout), .AC_i_2(AC[0]), .CLEAN(CLEAN));  // open: AC_i_1, AC_i_1_2
  Alublock_main main_2 (
    .AND(INP_7[0]), .ADD(INP_7[1]), .DR(INP_7[2]), .INPR(INP_7[3]), .COM(INP_7[4]), .SHR(INP_7[5]),
    .SHL(INP_7[6]), .DR_i(DR[1]), .AC_i(AC[1]), .Cin(main_1_cout), .INPR_I(INPR[1]), .LD(LOAD), .CLK(CLK),
    .Cout(main_2_cout), .AC_i_2(AC[1]), .CLEAN(CLEAN));  // open: AC_i_1, AC_i_1_2
  Alublock_main main_3 (
    .AND(INP_7[0]), .ADD(INP_7[1]), .DR(INP_7[2]), .INPR(INP_7[3]), .COM(INP_7[4]), .SHR(INP_7[5]),
    .SHL(INP_7[6]), .DR_i(DR[2]), .AC_i(AC[2]), .Cin(main_2_cout), .INPR_I(INPR[2]), .LD(LOAD), .CLK(CLK),
    .Cout(main_3_cout), .AC_i_2(AC[2]), .CLEAN(CLEAN));  // open: AC_i_1, AC_i_1_2
  Alublock_main main_4 (
    .AND(INP_7[0]), .ADD(INP_7[1]), .DR(INP_7[2]), .INPR(INP_7[3]), .COM(INP_7[4]), .SHR(INP_7[5]),
    .SHL(INP_7[6]), .DR_i(DR[3]), .AC_i(AC[3]), .Cin(main_3_cout), .INPR_I(INPR[3]), .LD(LOAD), .CLK(CLK),
    .Cout(main_4_cout), .AC_i_2(AC[3]), .CLEAN(CLEAN));  // open: AC_i_1, AC_i_1_2
  Alublock_main main_5 (
    .AND(INP_7[0]), .ADD(INP_7[1]), .DR(INP_7[2]), .INPR(INP_7[3]), .COM(INP_7[4]), .SHR(INP_7[5]),
    .SHL(INP_7[6]), .DR_i(DR[4]), .AC_i(AC[4]), .Cin(main_4_cout), .INPR_I(INPR[4]), .LD(LOAD), .CLK(CLK),
    .Cout(main_5_cout), .AC_i_2(AC[4]), .CLEAN(CLEAN));  // open: AC_i_1, AC_i_1_2
  Alublock_main main_6 (
    .AND(INP_7[0]), .ADD(INP_7[1]), .DR(INP_7[2]), .INPR(INP_7[3]), .COM(INP_7[4]), .SHR(INP_7[5]),
    .SHL(INP_7[6]), .DR_i(DR[5]), .AC_i(AC[5]), .Cin(main_5_cout), .INPR_I(INPR[5]), .LD(LOAD), .CLK(CLK),
    .Cout(main_6_cout), .AC_i_2(AC[5]), .CLEAN(CLEAN));  // open: AC_i_1, AC_i_1_2
  Alublock_main main_7 (
    .AND(INP_7[0]), .ADD(INP_7[1]), .DR(INP_7[2]), .INPR(INP_7[3]), .COM(INP_7[4]), .SHR(INP_7[5]),
    .SHL(INP_7[6]), .DR_i(DR[6]), .AC_i(AC[6]), .Cin(main_6_cout), .INPR_I(INPR[6]), .LD(LOAD), .CLK(CLK),
    .Cout(main_7_cout), .AC_i_2(AC[6]), .CLEAN(CLEAN));  // open: AC_i_1, AC_i_1_2
  Alublock_main main_8 (
    .AND(INP_7[0]), .ADD(INP_7[1]), .DR(INP_7[2]), .INPR(INP_7[3]), .COM(INP_7[4]), .SHR(INP_7[5]),
    .SHL(INP_7[6]), .DR_i(DR[7]), .AC_i(AC[7]), .Cin(main_7_cout), .INPR_I(INPR[7]), .LD(LOAD), .CLK(CLK),
    .Cout(main_8_cout), .AC_i_2(AC[7]), .CLEAN(CLEAN));  // open: AC_i_1, AC_i_1_2
  Alublock_main main_9 (
    .AND(INP_7[0]), .ADD(INP_7[1]), .DR(INP_7[2]), .INPR(INP_7[3]), .COM(INP_7[4]), .SHR(INP_7[5]),
    .SHL(INP_7[6]), .DR_i(DR[8]), .AC_i(AC[8]), .Cin(main_8_cout), .INPR_I(1'b0), .LD(LOAD), .CLK(CLK),
    .Cout(main_9_cout), .AC_i_2(AC[8]), .CLEAN(CLEAN));  // open: AC_i_1, AC_i_1_2
  Alublock_main main_10 (
    .AND(INP_7[0]), .ADD(INP_7[1]), .DR(INP_7[2]), .INPR(INP_7[3]), .COM(INP_7[4]), .SHR(INP_7[5]),
    .SHL(INP_7[6]), .DR_i(DR[9]), .AC_i(AC[9]), .Cin(main_9_cout), .INPR_I(1'b0), .LD(LOAD), .CLK(CLK),
    .Cout(main_10_cout), .AC_i_2(AC[9]), .CLEAN(CLEAN));  // open: AC_i_1, AC_i_1_2
  Alublock_main main_11 (
    .AND(INP_7[0]), .ADD(INP_7[1]), .DR(INP_7[2]), .INPR(INP_7[3]), .COM(INP_7[4]), .SHR(INP_7[5]),
    .SHL(INP_7[6]), .DR_i(DR[10]), .AC_i(AC[10]), .Cin(main_10_cout), .INPR_I(1'b0), .LD(LOAD), .CLK(CLK),
    .Cout(main_11_cout), .AC_i_2(AC[10]), .CLEAN(CLEAN));  // open: AC_i_1, AC_i_1_2
  Alublock_main main_12 (
    .AND(INP_7[0]), .ADD(INP_7[1]), .DR(INP_7[2]), .INPR(INP_7[3]), .COM(INP_7[4]), .SHR(INP_7[5]),
    .SHL(INP_7[6]), .DR_i(DR[11]), .AC_i(AC[11]), .Cin(main_11_cout), .INPR_I(1'b0), .LD(LOAD), .CLK(CLK),
    .Cout(main_12_cout), .AC_i_2(AC[11]), .CLEAN(CLEAN));  // open: AC_i_1, AC_i_1_2
  Alublock_main main_13 (
    .AND(INP_7[0]), .ADD(INP_7[1]), .DR(INP_7[2]), .INPR(INP_7[3]), .COM(INP_7[4]), .SHR(INP_7[5]),
    .SHL(INP_7[6]), .DR_i(DR[12]), .AC_i(AC[12]), .Cin(main_12_cout), .INPR_I(1'b0), .LD(LOAD), .CLK(CLK),
    .Cout(main_13_cout), .AC_i_2(AC[12]), .CLEAN(CLEAN));  // open: AC_i_1, AC_i_1_2
  Alublock_main main_14 (
    .AND(INP_7[0]), .ADD(INP_7[1]), .DR(INP_7[2]), .INPR(INP_7[3]), .COM(INP_7[4]), .SHR(INP_7[5]),
    .SHL(INP_7[6]), .DR_i(DR[13]), .AC_i(AC[13]), .Cin(main_13_cout), .INPR_I(1'b0), .LD(LOAD), .CLK(CLK),
    .Cout(main_14_cout), .AC_i_2(AC[13]), .CLEAN(CLEAN));  // open: AC_i_1, AC_i_1_2
  Alublock_main main_15 (
    .AND(INP_7[0]), .ADD(INP_7[1]), .DR(INP_7[2]), .INPR(INP_7[3]), .COM(INP_7[4]), .SHR(INP_7[5]),
    .SHL(INP_7[6]), .DR_i(DR[14]), .AC_i(AC[14]), .Cin(main_14_cout), .INPR_I(1'b0), .LD(LOAD), .CLK(CLK),
    .Cout(main_15_cout), .AC_i_2(AC[14]), .CLEAN(CLEAN));  // open: AC_i_1, AC_i_1_2
  Alublock_main main_16 (
    .AND(INP_7[0]), .ADD(INP_7[1]), .DR(INP_7[2]), .INPR(INP_7[3]), .COM(INP_7[4]), .SHR(INP_7[5]),
    .SHL(INP_7[6]), .DR_i(DR[15]), .AC_i(AC[15]), .Cin(main_15_cout), .INPR_I(1'b0), .LD(LOAD), .CLK(CLK),
    .AC_i_2(AC[15]), .CLEAN(CLEAN));  // open: AC_i_1, AC_i_1_2, Cout
endmodule
