// Logisim project Alublock.circ as structural Verilog: 1 circuit, main circuit main
// ALUBLOCK
module main (
  input  DR_i,
  input  AC_i_1,
  input  AC_i,
  input  AC_i_1_2,
  input  INPR_I,
  input  AND,
  input  Cin,
  input  ADD,
  input  LD,
  input  CLK,
  input  DR,
  input  INPR,
  input  CLEAN,
  input  COM,
  input  SHR,
  input  SHL,
  output Cout,
  output AC_i_2
);

  wire adder_1_out, and_1_out, and_2_out, and_3_out, and_4_out, and_5_out, and_6_out, and_7_out, and_8_out,
       and_9_out, not_1_out, not_2_out, or_1_out;

  Adder #(.width(1)) adder_1 (.a(DR_i), .b(AC_i), .out(adder_1_out), .cin(Cin), .cout(Cout));
  not not_1 (not_1_out, AC_i);
  and and_1 (and_1_out, AND, AC_i, DR_i);
  and and_2 (and_2_out, ADD, adder_1_out);
  and and_3 (and_3_out, DR, DR_i);
  and and_4 (and_4_out, INPR, INPR_I);
  and and_5 (and_5_out, COM, not_1_out);
  and and_6 (and_6_out, SHR, AC_i_1);
  and and_7 (and_7_out, SHL, AC_i_1_2);
  or or_1 (or_1_out, and_1_out, and_2_out, and_3_out, and_4_out, and_5_out, and_6_out, and_7_out);
  not not_2 (not_2_out, or_1_out);
  and and_8 (and_8_out, LD, or_1_out);
  and and_9 (and_9_out, LD, not_2_out);
  J_K_Flip_Flop j_k_ff_1 (.J(and_8_out), .clk(CLK), .K(and_9_out), .Q(AC_i_2), .reset(CLEAN));  // open: Qn, preset, en
endmodule
