// Logisim project main.circ as structural Verilog: 1 circuit, main circuit main
// I/O Ref
module main (
  input  FGO,
  input  FGI,
  input  clear,
  input  [7:0] INPR,
  input  Inc,
  input  clear_2,
  output R,
  output I,
  output [2:0] OPCODE,
  output [11:0] OPERAND,
  output IEN,
  output [2:0] out_12,
  output [15:0] AR,
  output [15:0] PC,
  output [15:0] DR,
  output E,
  output [15:0] AC,
  output [15:0] IR,
  output [15:0] TR,
  output [15:0] OUTR
);

  wire and_1_out, CLOCK_out, D7I_prime_T3_out, D7IT3_out, decoder_1_out0, decoder_1_out1, decoder_1_out2,
       decoder_1_out3, decoder_1_out4, decoder_1_out5, decoder_1_out6, decoder_1_out7, FGI_q, FGO_q,
       main_2_ac15, main_2_ac_val, main_2_dr_val, main_2_e_2, main_2_fgi_2, main_2_fgo_2, main_3_ien__0,
       main_3_ien__1, main_3_ld_ir, main_3_ld_tr, main_3_rj, main_3_rk, main_3_s__0, main_3_sc__0, not_1_out,
       not_2_out, not_3_out, S_q, SC_q, TIMER_t0, TIMER_t1, TIMER_t2, TIMER_t3, TIMER_t4, TIMER_t5, TIMER_t6,
       TIMER_t7;
  wire [1:0] main_3_e__e_prime, main_3_inc_ac, main_3_inc_dr, main_3_read;
  wire [2:0] main_3_inc_ar, main_3_inc_pc;
  wire [5:0] I_O_Ref_b6;
  wire [6:0] main_3_add;
  wire [11:0] Register_Ref_b0;
  wire [15:0] RAM_7_out;
  wire [20:0] Memory_Ref_r_prime_t0;

  counter_main TIMER (
    .Clock(and_1_out), .Clear(SC_q), .T0(TIMER_t0), .T1(TIMER_t1), .T2(TIMER_t2), .T3(TIMER_t3),
    .T4(TIMER_t4), .T5(TIMER_t5), .T6(TIMER_t6), .T7(TIMER_t7));
  Decoder #(.select(3)) decoder_1 (
    .out0(decoder_1_out0), .out1(decoder_1_out1), .out2(decoder_1_out2), .out3(decoder_1_out3),
    .out4(decoder_1_out4), .out5(decoder_1_out5), .out6(decoder_1_out6), .out7(decoder_1_out7),
    .sel(IR[14:12]));  // open: en
  not not_1 (not_1_out, I);
  and D7I_prime_T3 (D7I_prime_T3_out, decoder_1_out7, not_1_out, TIMER_t3);
  and D7IT3 (D7IT3_out, decoder_1_out7, I, TIMER_t3);
  ALU_main main_1 (
    .DR(DR), .INPR(INPR), .INP_7(main_3_add), .Eval(main_3_e__e_prime), .Inc(main_3_inc_ac[0]),
    .CLEAN(main_3_inc_ac[1]), .CLK(and_1_out), .E(E), .AC(AC));
  Register_Ref_main Register_Ref (
    .D7I_prime_T3(D7I_prime_T3_out), ._12bit_data(IR[11:0]), .B0(Register_Ref_b0[0]),
    .B1(Register_Ref_b0[1]), .B2(Register_Ref_b0[2]), .B3(Register_Ref_b0[3]), .B4(Register_Ref_b0[4]),
    .B5(Register_Ref_b0[5]), .B6(Register_Ref_b0[6]), .B7(Register_Ref_b0[7]), .B8(Register_Ref_b0[8]),
    .B9(Register_Ref_b0[9]), .B10(Register_Ref_b0[10]), .B11(Register_Ref_b0[11]));
  Input_Output_Ref_main I_O_Ref (
    .D7IT3(D7IT3_out), ._12bit_data(IR[11:0]), .B6(I_O_Ref_b6[0]), .B7(I_O_Ref_b6[1]), .B8(I_O_Ref_b6[2]),
    .B9(I_O_Ref_b6[3]), .B10(I_O_Ref_b6[4]), .B11(I_O_Ref_b6[5]));
  memory_main RAM_7 (
    .AC(AR[11:0]), .Data(OUTR), .Write(main_3_read[1]), .Clock(and_1_out), .Read(main_3_read[0]),
    .OUT(RAM_7_out));
  IncReg12_main AR_1 (
    .INP(OUTR[11:0]), .Inc(main_3_inc_ar[0]), .Load(main_3_inc_ar[1]), .Clear(main_3_inc_ar[2]),
    .OUT(AR[11:0]), .clock(and_1_out));
  IncReg12_main PC_2 (
    .INP(OUTR[11:0]), .Inc(main_3_inc_pc[0]), .Load(main_3_inc_pc[1]), .Clear(main_3_inc_pc[2]),
    .OUT(PC[11:0]), .clock(and_1_out));
  IncReg16_main DR_3 (
    .INP(OUTR), .Inc(main_3_inc_dr[0]), .Load(main_3_inc_dr[1]), .Clear(clear), .OUT(DR), .Clock(and_1_out));
  IR_main IR_5 (.inp(OUTR), .Load(main_3_ld_ir), .Clock(and_1_out), .out({I, IR[14:0]}));
  IncReg16_main TR_6 (.INP(OUTR), .Inc(Inc), .Load(main_3_ld_tr), .Clear(clear_2), .OUT(TR), .Clock(and_1_out));
  Memory_Ref_main Memory_Ref (
    .T0(TIMER_t0), .T1(TIMER_t1), .T2(TIMER_t2), .T3(TIMER_t3), .T4(TIMER_t4), .T5(TIMER_t5), .T6(TIMER_t6),
    .T7(TIMER_t7), .D0(decoder_1_out0), .D1(decoder_1_out1), .D2(decoder_1_out2), .D3(decoder_1_out3),
    .D4(decoder_1_out4), .D5(decoder_1_out5), .D6(decoder_1_out6), .D7(decoder_1_out7), .R(R), .IEN(IEN),
    .FGI(FGI), .FGO(FGO), .S(S_q), .E(E), .I(I), .R_prime_T0(Memory_Ref_r_prime_t0[0]),
    .R_prime_T1(Memory_Ref_r_prime_t0[1]), .R_prime_T2(Memory_Ref_r_prime_t0[2]),
    .D7_prime_IT3(Memory_Ref_r_prime_t0[3]),
    .T0_prime_T1_prime_T2_prime_IEN__FGO_FGI(Memory_Ref_r_prime_t0[4]), .RT0(Memory_Ref_r_prime_t0[5]),
    .RT1(Memory_Ref_r_prime_t0[6]), .RT2(Memory_Ref_r_prime_t0[7]), .D0T4(Memory_Ref_r_prime_t0[8]),
    .D0T5(Memory_Ref_r_prime_t0[9]), .D1T4(Memory_Ref_r_prime_t0[10]), .D1T5(Memory_Ref_r_prime_t0[11]),
    .D2T4(Memory_Ref_r_prime_t0[12]), .D2T5(Memory_Ref_r_prime_t0[13]), .D3T4(Memory_Ref_r_prime_t0[14]),
    .D4T4(Memory_Ref_r_prime_t0[15]), .D5T4(Memory_Ref_r_prime_t0[16]), .D5T5(Memory_Ref_r_prime_t0[17]),
    .D6T4(Memory_Ref_r_prime_t0[18]), .D6T5(Memory_Ref_r_prime_t0[19]), .D6T6(Memory_Ref_r_prime_t0[20]));
  and and_1 (and_1_out, CLOCK_out, not_2_out);
  Clock CLOCK (.out(CLOCK_out));
  D_Flip_Flop u_FGO (.clk(and_1_out), .D(FGO), .Q(FGO_q));  // open: Qn, preset, en, reset
  D_Flip_Flop u_FGI (.clk(and_1_out), .D(FGI), .Q(FGI_q));  // open: Qn, preset, en, reset
  not not_2 (not_2_out, S_q);
  val_extract_main main_2 (
    .DR(DR), .AC(AC), .E(E), .FGO(FGO_q), .FGI(FGI_q), .AC_Val(main_2_ac_val), .DR_Val(main_2_dr_val),
    .AC15(main_2_ac15), .E_2(main_2_e_2), .FGO_2(main_2_fgo_2), .FGI_2(main_2_fgi_2));
  MAINLOGIC_main main_3 (
    .AC_Val(main_2_ac_val), .DR(main_2_dr_val), .AC15(main_2_ac15), .E(main_2_e_2), .FGO(main_2_fgo_2),
    .FGI(main_2_fgi_2), .R_prime_T0(Memory_Ref_r_prime_t0[0]), .R_prime_T1(Memory_Ref_r_prime_t0[1]),
    .R_prime_T2(Memory_Ref_r_prime_t0[2]), .D7_prime_IT3(Memory_Ref_r_prime_t0[3]),
    .T1_prime_T2_prime_T3_prime(Memory_Ref_r_prime_t0[4]), .RT0(Memory_Ref_r_prime_t0[5]),
    .RT1(Memory_Ref_r_prime_t0[6]), .RT2(Memory_Ref_r_prime_t0[7]), .D0T4(Memory_Ref_r_prime_t0[8]),
    .D0T5(Memory_Ref_r_prime_t0[9]), .D1T4(Memory_Ref_r_prime_t0[10]), .D1T5(Memory_Ref_r_prime_t0[11]),
    .D2T4(Memory_Ref_r_prime_t0[12]), .D2T5(Memory_Ref_r_prime_t0[13]), .D3T4(Memory_Ref_r_prime_t0[14]),
    .D4T4(Memory_Ref_r_prime_t0[15]), .D5T4(Memory_Ref_r_prime_t0[16]), .D5T5(Memory_Ref_r_prime_t0[17]),
    .D6T4(Memory_Ref_r_prime_t0[18]), .D6T5(Memory_Ref_r_prime_t0[19]), .D6T6(Memory_Ref_r_prime_t0[20]),
    .rB0(Register_Ref_b0[0]), .rB1(Register_Ref_b0[1]), .rB2(Register_Ref_b0[2]), .rB3(Register_Ref_b0[3]),
    .rB4(Register_Ref_b0[4]), .rB5(Register_Ref_b0[5]), .rB6(Register_Ref_b0[6]), .rB7(Register_Ref_b0[7]),
    .rB8(Register_Ref_b0[8]), .rB9(Register_Ref_b0[9]), .rB10(Register_Ref_b0[10]),
    .rB11(Register_Ref_b0[11]), .pB6(I_O_Ref_b6[0]), .pB7(I_O_Ref_b6[1]), .pB8(I_O_Ref_b6[2]),
    .pB9(I_O_Ref_b6[3]), .pB10(I_O_Ref_b6[4]), .pB11(I_O_Ref_b6[5]), .INC_AR(main_3_inc_ar[0]),
    .LD_AR(main_3_inc_ar[1]), .CLR_AR(main_3_inc_ar[2]), .RJ(main_3_rj), .Rk(main_3_rk),
    .INC_PC(main_3_inc_pc[0]), .LD_PC(main_3_inc_pc[1]), .CLR_PC(main_3_inc_pc[2]), .READ(main_3_read[0]),
    .WRITE(main_3_read[1]), .INC_DR(main_3_inc_dr[0]), .LD_DR(main_3_inc_dr[1]), .LD_IR(main_3_ld_ir),
    .LD_TR(main_3_ld_tr), .INC_AC(main_3_inc_ac[0]), .CLR_AC(main_3_inc_ac[1]), .S0(out_12[0]),
    .S1(out_12[1]), .S2(out_12[2]), .S__0(main_3_s__0), .ADD(main_3_add[0]), .AND(main_3_add[1]),
    .DR_2(main_3_add[2]), .INPR(main_3_add[3]), .COM(main_3_add[4]), .SHR(main_3_add[5]),
    .SHL(main_3_add[6]), .E__E_prime(main_3_e__e_prime[0]), .E__0(main_3_e__e_prime[1]),
    .SC__0(main_3_sc__0), .IEN__0(main_3_ien__0), .IEN__1(main_3_ien__1));
  not not_3 (not_3_out, main_3_sc__0);
  Multiplexer #(.select(3), .width(16)) multiplexer_1 (
    .in1(AR), .in2(PC), .in3(DR), .in4(AC), .in5({I, IR[14:0]}), .in6(TR), .in7(RAM_7_out), .out(OUTR),
    .sel(out_12));  // open: in0, en
  D_Flip_Flop S (.clk(and_1_out), .D(main_3_s__0), .Q(S_q));  // open: Qn, preset, en, reset
  J_K_Flip_Flop SC (.J(main_3_sc__0), .clk(and_1_out), .K(not_3_out), .Q(SC_q));  // open: Qn, preset, en, reset
  J_K_Flip_Flop R_FLAG (.J(main_3_rj), .clk(and_1_out), .K(main_3_rk), .Q(R));  // open: Qn, preset, en, reset
  J_K_Flip_Flop IEN_FLAG (
    .J(main_3_ien__0), .clk(and_1_out), .K(main_3_ien__1), .Q(IEN));  // open: Qn, preset, en, reset

  assign IR[15] = I;
  assign OPCODE = IR[14:12];
  assign OPERAND = IR[11:0];
endmodule
