// Logisim project memory.circ as structural Verilog: 1 circuit, main circuit main
module main (
  input  [11:0] AC,
  input  [15:0] Data,
  input  Write,
  input  Read,
  input  Clock,
  output [15:0] OUT
);

  RAM #(.addrWidth(12), .dataWidth(16), .bus("separate")) ram_1 (
    .addr(AC), .din(Data), .data(OUT), .str(Write), .clk(Clock), .ld(Read));  // open: sel, clr
endmodule
