// Logisim project val-extract.circ as structural Verilog: 1 circuit, main circuit main
module main (
  input  [15:0] DR,
  input  [15:0] AC,
  input  E,
  input  FGO,
  input  FGI,
  output AC_Val,
  output DR_Val,
  output AC15,
  output E_2,
  output FGO_2,
  output FGI_2
);

  or or_1 (DR_Val, DR[0], DR[0], DR[1], DR[2], DR[3], DR[4], DR[5], DR[6], DR[7], DR[8], DR[9], DR[10], DR[11], DR[12], DR[13], DR[14], DR[15]);
  or or_2 (AC_Val, AC[0], AC[0], AC[1], AC[2], AC[3], AC[4], AC[5], AC[6], AC[7], AC[8], AC[9], AC[10], AC[11], AC[12], AC[13], AC[14], AC[15]);

  assign AC15 = AC[15];
  assign E_2 = E;
  assign FGI_2 = FGI;
  assign FGO_2 = FGO;
endmodule
